# Fritzing sketch ardBeeQueenFritz (saved by Fritzing 0.9.2b)

parts:
  Part1 = Arduino Pro Mini v13
  DS1 = DS18B20 1-Wire Temperature Sensor [part_number=DS18B20]  # not connected
  Part2 = KY-019 5V Relay Module [package="Breakout board"]  # not connected
  R1 = Resistor [tolerance=±5% resistance=4.7k package=THT]  # not connected
  X1 = USB Connectors [package=usb-microb]

nets:
  N1: Part1.RAW, X1.VBUS
  GND: Part1.GND, X1.GND

custom parts:
  KY-019 5V Relay Module: KY-019 5V Relay module, used to control AC circuits.
